// Digital circuit SOP.dig as structural Verilog
module SOP (
  input  A,
  input  D,
  output out_3
);

  wire not_1_out, not_2_out, or_1_out, or_2_out;

  not not_1 (not_1_out, A);
  not not_2 (not_2_out, D);
  or or_1 (or_1_out, A, D);
  or or_2 (or_2_out, not_1_out, not_2_out);
  and and_1 (out_3, or_1_out, or_2_out);

  // Notes on the sheet:
  //   A: MSB
  //   D: LSB
  //   Use A as the most-significant bit and 
  //   D as the least-significant bit.
endmodule

/* Test case:
A B C D Y
0 0 0 0 X
0 0 0 1 1
*/
